# Fritzing sketch wiringLeds (saved by Fritzing 0.9.3b)
breadboards: 1

parts:
  R1 = BBC MicroBit
  J1 = Piezo Speaker
  LED1 = LED - 5mm [color="Green (570nm)" package="5 mm [THT]"]
  LED2 = LED - 5mm [color="Red (633nm)" package="5 mm [THT]"]
  LED3 = LED - 5mm [color="Orange (620nm)" package="5 mm [THT]"]
  R2 = Resistor [tolerance=±5% resistance=47 package=THT]
  R3 = Resistor [tolerance=±5% resistance=47 package=THT]
  R4 = Resistor [tolerance=±5% resistance=47 package=THT]

nets:
  N1: R1.GND, J1.pin2, LED1.cathode, LED2.cathode, LED3.cathode
  N2: R1.P16, R4.Pin_0
  N3: R1.P2_-_ANALOG_IN, R3.Pin_0
  N4: R1.P1_ANALOG_IN, R2.Pin_1
  N5: R1.P0_ANALOG_IN, J1.pin1
  N6: LED1.anode, R3.Pin_1
  N7: LED2.anode, R4.Pin_1
  N8: LED3.anode, R2.Pin_0

custom parts:
  BBC MicroBit: The BBC MICRO:BIT
